# Fritzing sketch MIDi_To_Fan_layout (saved by Fritzing 0.6.3b)
breadboards: 1

parts:
  Arduino1 = Arduino
  MIDI-_Input = DIN-5 jack (MIDI) [package=THT]
  R1 = Resistor [tolerance=±5% resistance=220 package=THT]
  D1 = Rectifier Diode [part_number=1N4001 package="300 mil [THT]"]
  R2 = Resistor [tolerance=±5% resistance=270 package=THT]
  Optocoppler = IC, DIP package, 8 pins [chip_label="6N 138 " spacing=300mil]
  SPKR1 = Loudspeaker
  VCC_for_SPKRs = Battery block 9V
  SPKR2 = Loudspeaker
  R3 = Resistor [tolerance=±5% resistance=990 package=THT]
  R4 = Resistor [tolerance=±5% resistance=990 package=THT]
  Q1 = NPN-Transistor [package="TO92 [THT]"]
  Q2 = NPN-Transistor [package="TO92 [THT]"]

nets:
  GND: Arduino1.GND, Optocoppler.pin5, VCC_for_SPKRs.-, Q1.E, Q2.E
  N1: Arduino1.D8, R4.Pin_1
  N2: Arduino1.D4, R3.Pin_1
  N3: Arduino1.D0RX, R2.Pin_1, Optocoppler.pin6
  N4: Arduino1.+5V, R2.Pin_0, Optocoppler.pin8
  N5: MIDI-_Input.5, D1.cathode, Optocoppler.pin2
  N6: MIDI-_Input.4, R1.Pin_1
  N7: R1.Pin_0, D1.anode, Optocoppler.pin3
  N8: SPKR1.pin1, Q1.C
  N9: SPKR1.pin2, VCC_for_SPKRs.+, SPKR2.pin2
  N10: SPKR2.pin1, Q2.C
  N11: R3.Pin_0, Q2.B
  N12: R4.Pin_0, Q1.B
